# Fritzing sketch ArduinoDiagram (saved by Fritzing 0.9.5d)
breadboards: 1

parts:
  Raspberry_Pi_1 = Raspberry Pi 3 [part_number=RPI-3-V1.2]  # not connected
  U1 = TOUCH [package=touch1]
  R1 = Resistor [tolerance=±5% resistance=220 package=THT]
  LED1 = smd LED [color="Red (633nm)" package="1206 [SMD]"]
  ADC1 = MCP3008 [package=dil16]
  Part1 = Sound Sensor Module
  Mod1 = Flame Sensor Module [package="Breakout board"]

nets:
  N1: U1.T2, Part1.VCC, Mod1.+
  N2: R1.Pin_0, Part1.GND, Mod1.G
  N3: R1.Pin_1, LED1.cathode
  N4: ADC1.CS/SHDN, Mod1.A0
  N5: ADC1.AGND, Part1.OUT

notes:
  MQ7
  p- GNO
  blu-GCC
  w- DO
  g- AO
  Water sensor
  bla- negative
  w- positive
  bro- S
  temp and humidity
  GND- w
  DATA- g
  VCC-r

custom parts:
  Sound Sensor Module: Sound sensor module can detect not only sound, but also the sound or special frequency. It can be adjusted via the blue Potentiometer. This sensor module can work under 3.3V and 5V When the module detect the sound below value of the code, D0 pin of the module will output high level. Else, D0 will output low level.
  Flame Sensor Module: KY-026 Flame Sensor Module reacts in the presence of fire.
